# Fritzing sketch circuitSchema (saved by Fritzing 0.9.3b)
breadboards: 1

parts:
  Reset = Pushbutton [package="[THT]"]
  Arduino_Uno = Arduino Uno (Rev3)
  White_sensor = LHi958 [package=to-39]
  Y_- = Pushbutton [package="[THT]"]
  R2 = Resistor [tolerance=±5% resistance=10k package=THT]
  Y_+ = Pushbutton [package="[THT]"]
  R3 = Resistor [tolerance=±5% resistance=10k package=THT]
  W_- = Pushbutton [package="[THT]"]
  R4 = Resistor [tolerance=±5% resistance=10k package=THT]
  W_+ = Pushbutton [package="[THT]"]
  R5 = Resistor [tolerance=±5% resistance=10k package=THT]
  R6 = Resistor [tolerance=±5% resistance=10k package=THT]
  Lights = Pushbutton [package="[THT]"]
  Yellow_sensor = LHi958 [package=to-39]
  WS2813_strip = ws2812b [package="smd 2812b"]
  Buzzer = Piezo Speaker
  R7 = Resistor [tolerance=±5% resistance=10k package=THT]

nets:
  5V: Reset.Pin_1, Reset.Pin_2, Arduino_Uno.5V, White_sensor.n.a., Y_-.Pin_1, Y_-.Pin_2, Y_+.Pin_3, Y_+.Pin_4, W_-.Pin_1, W_-.Pin_2, W_+.Pin_3, W_+.Pin_4, Lights.Pin_1, Lights.Pin_2, Yellow_sensor.n.a., WS2813_strip.VDD
  N1: Reset.Pin_3, Reset.Pin_4, Arduino_Uno.D2, R7.Pin_0
  N2: Arduino_Uno.D8, White_sensor.D
  N3: Arduino_Uno.D9_PWM, Yellow_sensor.D
  N4: Arduino_Uno.D10_PWM/SS, WS2813_strip.DIN
  N5: Arduino_Uno.D11_PWM/MOSI, Buzzer.pin2
  N6: Arduino_Uno.D3_PWM, Y_-.Pin_3, Y_-.Pin_4, R2.Pin_1
  N7: Arduino_Uno.D4, Y_+.Pin_1, Y_+.Pin_2, R3.Pin_0
  N8: Arduino_Uno.D5_PWM, W_-.Pin_3, W_-.Pin_4, R4.Pin_1
  N9: Arduino_Uno.D6_PWM, W_+.Pin_1, W_+.Pin_2, R5.Pin_0
  N10: Arduino_Uno.D7, R6.Pin_1, Lights.Pin_3, Lights.Pin_4
  GND: Arduino_Uno.GND, White_sensor.GND, R2.Pin_0, R3.Pin_1, R4.Pin_0, R5.Pin_1, R6.Pin_0, Yellow_sensor.GND, WS2813_strip.VSS, Buzzer.pin1, R7.Pin_1
